// Logisim project CPU.circ as structural Verilog: 5 circuits, main circuit main
module main (
  output [15:0] out_1,
  output [15:0] out_2,
  output [15:0] out_3
);

  wire alu_1_first_smaller_or_equal, alu_1_not_equal, ALUsrc, and_1_out, and_2_out, and_3_out, ble, bne,
       call, clk, halt, j, li, MemRead, MemToReg, MemWrite, move, not_1_out, not_2_out, or_1_out, or_2_out,
       RegDst, RegWrite, rtn;
  wire [1:0] ALUop;
  wire [2:0] multiplexer_2_out;
  wire [3:0] opcode;
  wire [11:0] rom_1_data;
  wire [15:0] adder_1_out, adder_2_out, alu_1_alu_output, bit_extender_1_out, bit_extender_2_out,
       multiplexer_1_out, multiplexer_3_out, multiplexer_6_out, multiplexer_7_out, multiplexer_8_out, ra_q,
       ram_1_data, register_1_q, register_file_1_data2;

  Register #(.width(16)) register_1 (.D(multiplexer_1_out), .en(not_1_out), .Q(register_1_q), .clk(clk));  // open: clr
  not not_1 (not_1_out, halt);
  Clock clock_1 (.out(clk));
  Control Control (
    .A(opcode[3]), .B(opcode[2]), .C(opcode[1]), .D(opcode[0]), .RegDst(RegDst), .move(move),
    .ALUsrc(ALUsrc), .li(li), .MemWrite(MemWrite), .MemRead(MemRead), .MemToReg(MemToReg), .ble(ble),
    .bne(bne), .j(j), .rtn(rtn), .call(call), .RegWrite(RegWrite), .ALUop(ALUop), .halt(halt));
  Multiplexer #(.width(16), .enable("false")) multiplexer_1 (
    .in0(multiplexer_7_out), .in1(ra_q), .out(multiplexer_1_out), .sel(rtn));
  Adder #(.width(16)) adder_1 (.a(16'h1), .b(register_1_q), .out(adder_1_out));  // open: cin, cout
  ROM #(.addrWidth(16), .dataWidth(16)) rom_1 (.addr(register_1_q), .data({opcode, rom_1_data}));  // open: sel
  not not_2 (not_2_out, halt);
  and and_1 (and_1_out, call, not_2_out);
  Register #(.width(16)) ra (.D(adder_1_out), .en(and_1_out), .Q(ra_q), .clk(clk), .clr(halt));
  assign bit_extender_1_out = {{4{rom_1_data[11]}}, rom_1_data};  // Bit_Extender bit_extender_1
  assign bit_extender_2_out = {{10{rom_1_data[5]}}, rom_1_data[5:0]};  // Bit_Extender bit_extender_2
  Multiplexer #(.width(3), .enable("false")) multiplexer_2 (
    .in0(rom_1_data[8:6]), .in1(rom_1_data[5:3]), .out(multiplexer_2_out), .sel(RegDst));
  register_file register_file_1 (
    .Write(RegWrite), .Write_Register(multiplexer_2_out), .Register_Data(out_1), .clock(clk), .Data1(out_2),
    .Data2(register_file_1_data2), .reset(halt), .Read_Regisiter2(rom_1_data[8:6]),
    .Read_Regisiter1(rom_1_data[11:9]));
  Multiplexer #(.width(16), .enable("false")) multiplexer_3 (
    .in0(bit_extender_2_out), .in1(bit_extender_1_out), .out(multiplexer_3_out), .sel(or_1_out));
  or or_1 (or_1_out, j, call);
  Multiplexer #(.width(16), .enable("false")) multiplexer_4 (
    .in0(out_2), .in1(multiplexer_6_out), .out(out_1), .sel(move));
  Multiplexer #(.width(16), .enable("false")) multiplexer_5 (
    .in0(register_file_1_data2), .in1(bit_extender_2_out), .out(out_3), .sel(ALUsrc));
  Adder #(.width(16)) adder_2 (.a(register_1_q), .b(multiplexer_3_out), .out(adder_2_out));  // open: cin, cout
  Multiplexer #(.width(16), .enable("false")) multiplexer_6 (
    .in0(multiplexer_8_out), .in1(bit_extender_2_out), .out(multiplexer_6_out), .sel(li));
  ALU alu_1 (
    .input_1(out_2), .input_2(out_3), .ALUcontrol(ALUop), .not_equal(alu_1_not_equal),
    .first_smaller_or_equal(alu_1_first_smaller_or_equal), .ALU_output(alu_1_alu_output));
  and and_2 (and_2_out, bne, alu_1_not_equal);
  and and_3 (and_3_out, ble, alu_1_first_smaller_or_equal);
  or or_2 (or_2_out, and_2_out, or_1_out, and_3_out);
  Multiplexer #(.width(16), .enable("false")) multiplexer_7 (
    .in0(adder_1_out), .in1(adder_2_out), .out(multiplexer_7_out), .sel(or_2_out));
  RAM #(.addrWidth(16), .dataWidth(16), .bus("separate")) ram_1 (
    .addr(alu_1_alu_output), .din(register_file_1_data2), .data(ram_1_data), .str(MemWrite), .clk(clk),
    .ld(MemRead));  // open: sel, clr
  Multiplexer #(.width(16), .enable("false")) multiplexer_8 (
    .in0(ram_1_data), .in1(alu_1_alu_output), .out(multiplexer_8_out), .sel(MemToReg));

  // Notes on the sheet:
  //   contents of rom_1 (hex, n*v repeats v):
  //   6 44 d007 64c0 7 48 d003 6500 c003 1050 e000 f000
endmodule

module register_file (
  input  Write,
  input  [2:0] Write_Register,
  input  [2:0] Read_Regisiter2,
  input  [2:0] Read_Regisiter1,
  input  reset,
  input  [15:0] Register_Data,
  input  clock,
  output [15:0] Data1,
  output [15:0] Data2
);

  wire and_1_out, and_2_out, and_3_out, and_4_out, and_5_out, and_6_out, and_7_out, and_8_out,
       decoder_1_out0, decoder_1_out1, decoder_1_out2, decoder_1_out3, decoder_1_out4, decoder_1_out5,
       decoder_1_out6, decoder_1_out7;
  wire [15:0] register_1_q, register_2_q, register_3_q, register_4_q, register_5_q, register_6_q,
       register_7_q, register_8_q;

  Decoder #(.select(3), .enable("false")) decoder_1 (
    .out0(decoder_1_out0), .out1(decoder_1_out1), .out2(decoder_1_out2), .out3(decoder_1_out3),
    .out4(decoder_1_out4), .out5(decoder_1_out5), .out6(decoder_1_out6), .out7(decoder_1_out7),
    .sel(Write_Register));
  and and_1 (and_1_out, Write, decoder_1_out0);
  and and_2 (and_2_out, Write, decoder_1_out1);
  and and_3 (and_3_out, Write, decoder_1_out2);
  and and_4 (and_4_out, Write, decoder_1_out3);
  and and_5 (and_5_out, Write, decoder_1_out4);
  and and_6 (and_6_out, Write, decoder_1_out5);
  and and_7 (and_7_out, Write, decoder_1_out6);
  and and_8 (and_8_out, Write, decoder_1_out7);
  Register #(.width(16)) register_1 (.D(Register_Data), .en(and_1_out), .Q(register_1_q), .clk(clock), .clr(reset));
  Register #(.width(16)) register_2 (.D(Register_Data), .en(and_2_out), .Q(register_2_q), .clk(clock), .clr(reset));
  Register #(.width(16)) register_3 (.D(Register_Data), .en(and_3_out), .Q(register_3_q), .clk(clock), .clr(reset));
  Register #(.width(16)) register_4 (.D(Register_Data), .en(and_4_out), .Q(register_4_q), .clk(clock), .clr(reset));
  Register #(.width(16)) register_5 (.D(Register_Data), .en(and_5_out), .Q(register_5_q), .clk(clock), .clr(reset));
  Register #(.width(16)) register_6 (.D(Register_Data), .en(and_6_out), .Q(register_6_q), .clk(clock), .clr(reset));
  Register #(.width(16)) register_7 (.D(Register_Data), .en(and_7_out), .Q(register_7_q), .clk(clock), .clr(reset));
  Register #(.width(16)) register_8 (.D(Register_Data), .en(and_8_out), .Q(register_8_q), .clk(clock), .clr(reset));
  Multiplexer #(.select(3), .width(16), .enable("false")) multiplexer_1 (
    .in0(register_1_q), .in1(register_2_q), .in2(register_3_q), .in3(register_4_q), .in4(register_5_q),
    .in5(register_6_q), .in6(register_7_q), .in7(register_8_q), .out(Data2), .sel(Read_Regisiter2));
  Multiplexer #(.select(3), .width(16), .enable("false")) multiplexer_2 (
    .in0(register_1_q), .in1(register_2_q), .in2(register_3_q), .in3(register_4_q), .in4(register_5_q),
    .in5(register_6_q), .in6(register_7_q), .in7(register_8_q), .out(Data1), .sel(Read_Regisiter1));
endmodule

module ALU (
  input  [15:0] input_1,
  input  [15:0] input_2,
  input  [1:0] ALUcontrol,
  output not_equal,
  output first_smaller_or_equal,
  output [15:0] ALU_output
);

  wire comparator_1_eq, comparator_1_lt;
  wire [15:0] adder_1_out, and_1_out, or_1_out;

  Adder #(.width(16)) adder_1 (.a(input_1), .b(input_2), .out(adder_1_out));  // open: cin, cout
  Comparator #(.width(16)) comparator_1 (
    .a(input_1), .b(input_2), .eq(comparator_1_eq), .lt(comparator_1_lt));  // open: gt
  assign and_1_out = input_2 & input_1;  // AND_Gate and_1, 16 bits wide
  assign or_1_out = input_2 | input_1;  // OR_Gate or_1, 16 bits wide
  not not_1 (not_equal, comparator_1_eq);
  or or_2 (first_smaller_or_equal, comparator_1_eq, comparator_1_lt);
  Multiplexer #(.select(2), .width(16), .enable("false")) multiplexer_1 (
    .in0(adder_1_out), .in1(and_1_out), .in2(or_1_out), .out(ALU_output), .sel(ALUcontrol));  // open: in3
endmodule

module Bit_concat (
  input  bit1,
  input  bit2,
  output [1:0] \output 
);

  wire [1:0] bit_extender_1_out, bit_extender_2_out, shifter_1_out;

  assign bit_extender_1_out = {{1{1'b0}}, bit1};  // Bit_Extender bit_extender_1
  assign bit_extender_2_out = {{1{1'b0}}, bit2};  // Bit_Extender bit_extender_2
  Shifter #(.width(2)) shifter_1 (.in(bit_extender_1_out), .\dist (1'b1), .out(shifter_1_out));
  Adder #(.width(2)) adder_1 (.a(shifter_1_out), .b(bit_extender_2_out), .out(\output ));  // open: cin, cout
endmodule

module Control (
  input  A,
  input  B,
  input  C,
  input  D,
  output RegDst,
  output move,
  output ALUsrc,
  output li,
  output MemWrite,
  output MemRead,
  output MemToReg,
  output ble,
  output bne,
  output j,
  output rtn,
  output call,
  output RegWrite,
  output [1:0] ALUop,
  output halt
);

  wire and_1_out, and_2_out, and_3_out, and_4_out, and_5_out, and_6_out, and_7_out, and_8_out, and_9_out,
       and_10_out, and_11_out, and_12_out, and_13_out, and_14_out, and_15_out, and_16_out, and_17_out,
       and_27_out, and_28_out, and_29_out, and_30_out, not_1_out, not_2_out, not_3_out, not_4_out, not_5_out,
       not_6_out, not_7_out, not_8_out, not_9_out, not_10_out, not_11_out, not_12_out, not_13_out,
       not_14_out, not_15_out, not_16_out, not_17_out, not_18_out, not_19_out, not_20_out, not_21_out,
       not_22_out, not_23_out, not_24_out, not_25_out, not_26_out, not_27_out, not_28_out, not_29_out,
       not_30_out, not_31_out, not_32_out, not_33_out, not_34_out, not_35_out, not_36_out, not_37_out,
       not_38_out, not_39_out, not_40_out, not_41_out, not_42_out, not_43_out, not_44_out, not_45_out,
       not_46_out, not_47_out, not_48_out, not_49_out, not_50_out, not_51_out, not_52_out, not_53_out,
       not_54_out, not_55_out, not_56_out, not_57_out, or_6_out, or_7_out;

  not not_1 (not_1_out, A);
  not not_2 (not_2_out, B);
  and and_1 (and_1_out, not_1_out, not_2_out, D);
  not not_3 (not_3_out, A);
  not not_4 (not_4_out, B);
  and and_2 (and_2_out, not_3_out, not_4_out, C);
  not not_5 (not_5_out, A);
  and and_3 (and_3_out, not_5_out, not_6_out);
  not not_6 (not_6_out, B);
  not not_7 (not_7_out, A);
  and and_4 (and_4_out, not_7_out, not_8_out, not_9_out);
  not not_8 (not_8_out, C);
  not not_9 (not_9_out, D);
  not not_10 (not_10_out, B);
  and and_5 (and_5_out, not_10_out, not_11_out);
  not not_11 (not_11_out, C);
  not not_12 (not_12_out, A);
  and and_6 (and_6_out, not_12_out, C, D);
  not not_13 (not_13_out, A);
  and and_7 (and_7_out, not_13_out, B, not_14_out);
  not not_14 (not_14_out, C);
  not not_15 (not_15_out, A);
  and and_8 (and_8_out, not_15_out, B, D);
  and and_9 (and_9_out, A, not_16_out, not_17_out);
  not not_16 (not_16_out, B);
  not not_17 (not_17_out, C);
  not not_18 (not_18_out, A);
  not not_19 (not_19_out, B);
  not not_20 (not_20_out, C);
  not not_21 (not_21_out, D);
  not not_22 (not_22_out, A);
  not not_23 (not_23_out, C);
  not not_24 (not_24_out, A);
  not not_25 (not_25_out, C);
  not not_26 (not_26_out, D);
  not not_27 (not_27_out, A);
  not not_28 (not_28_out, B);
  and and_10 (and_10_out, not_27_out, not_28_out, D);
  not not_29 (not_29_out, A);
  and and_11 (and_11_out, not_29_out, not_30_out, C);
  not not_30 (not_30_out, B);
  not not_31 (not_31_out, A);
  and and_12 (and_12_out, not_31_out, C, D);
  and and_13 (and_13_out, A, not_32_out, not_33_out);
  not not_32 (not_32_out, B);
  not not_33 (not_33_out, C);
  not not_34 (not_34_out, B);
  not not_35 (not_35_out, D);
  not not_36 (not_36_out, B);
  not not_37 (not_37_out, C);
  not not_38 (not_38_out, D);
  not not_39 (not_39_out, D);
  not not_40 (not_40_out, C);
  not not_41 (not_41_out, A);
  and and_14 (and_14_out, not_41_out, not_42_out);
  not not_42 (not_42_out, B);
  not not_43 (not_43_out, A);
  and and_15 (and_15_out, not_43_out, not_44_out);
  not not_44 (not_44_out, D);
  not not_45 (not_45_out, B);
  and and_16 (and_16_out, not_45_out, not_46_out);
  not not_46 (not_46_out, C);
  not not_47 (not_47_out, A);
  and and_17 (and_17_out, not_47_out, C);
  not not_48 (not_48_out, A);
  not not_49 (not_49_out, B);
  not not_50 (not_50_out, B);
  not not_51 (not_51_out, C);
  not not_52 (not_52_out, A);
  not not_53 (not_53_out, B);
  not not_54 (not_54_out, D);
  not not_55 (not_55_out, B);
  not not_56 (not_56_out, C);
  not not_57 (not_57_out, D);
  and and_18 (halt, A, B, C, D);
  or or_1 (RegDst, and_1_out, and_2_out);
  or or_2 (move, and_3_out, and_4_out, and_5_out, and_6_out);
  or or_3 (ALUsrc, and_7_out, and_8_out, and_9_out);
  and and_19 (li, not_18_out, not_19_out, not_20_out, not_21_out);
  and and_20 (MemWrite, not_22_out, B, not_23_out, D);
  and and_21 (MemRead, not_24_out, B, not_25_out, not_26_out);
  or or_4 (MemToReg, and_10_out, and_11_out, and_12_out, and_13_out);
  and and_22 (ble, A, not_34_out, C, not_35_out);
  and and_23 (bne, A, not_36_out, C, D);
  and and_24 (j, A, B, not_37_out, not_38_out);
  and and_25 (rtn, A, B, C, not_39_out);
  and and_26 (call, A, B, not_40_out, D);
  or or_5 (RegWrite, and_14_out, and_15_out, and_16_out, and_17_out);
  and and_27 (and_27_out, not_48_out, not_49_out, C, D);
  or or_6 (or_6_out, and_27_out, and_28_out);
  and and_28 (and_28_out, A, not_50_out, not_51_out, D);
  and and_29 (and_29_out, not_52_out, not_53_out, C, not_54_out);
  or or_7 (or_7_out, and_29_out, and_30_out);
  and and_30 (and_30_out, A, not_55_out, not_56_out, not_57_out);
  Bit_concat bit_concat_1 (.bit1(or_6_out), .bit2(or_7_out), .\output (ALUop));
endmodule
